# Fritzing sketch Project_12 (saved by Fritzing 0.8.7b)
breadboards: 1

parts:
  Part1 = Adafruit Feather HUZZAH ESP8266 [part_number="Adafruit #2821"]
  LED1 = LED - 5mm [color="Red (633nm)" package="5 mm [THT]"]
  LED2 = LEDs [package=led10mm]
  LED3 = LEDs [package=led10mm]
  LED4 = LEDs [package=led10mm]
  S1 = Pushbutton [package="[THT]"]
  S2 = Pushbutton [package="[THT]"]
  S3 = Pushbutton [package="[THT]"]
  S4 = Pushbutton [package="[THT]"]
  J1 = Piezo Speaker
  R1 = Resistor [package="2010 [SMD]"]
  R2 = Resistor [tolerance=±5% resistance=220 package=THT]
  R3 = Resistor [tolerance=±5% resistance=220 package=THT]
  R4 = Resistor [tolerance=±5% resistance=220 package=THT]
  R5 = Resistor [package="2010 [SMD]"]
  R6 = Resistor [package="2010 [SMD]"]
  R7 = Resistor [package="2010 [SMD]"]
  R9 = Resistor [package="2010 [SMD]"]
  R8 = Resistor [package="2010 [SMD]"]

nets:
  N1: Part1.GPIO12/MISO, R1.Pin_1
  N2: Part1.GPIO13/MOSI, R2.Pin_1
  N3: Part1.GPIO14/SCK, R3.Pin_1
  N4: Part1.GND, LED1.anode, LED2.C, LED3.C, LED4.C, J1.pin1, R5.Pin_1, R6.Pin_1, R7.Pin_1, R8.Pin_1
  N5: Part1.3.3V, S1.Pin_3, S1.Pin_4, S2.Pin_3, S2.Pin_4, S3.Pin_3, S3.Pin_4, S4.Pin_3, S4.Pin_4
  N6: Part1.GPIO15, S3.Pin_1, S3.Pin_2, R6.Pin_0
  N7: Part1.GPIO16, R9.Pin_1
  N8: Part1.GPIO5/SCL, S2.Pin_1, S2.Pin_2, R7.Pin_0
  N9: Part1.GPIO4/SDA, S1.Pin_1, S1.Pin_2, R5.Pin_0
  N10: LED1.cathode, R2.Pin_0
  N11: LED2.A, R1.Pin_0
  N12: LED3.A, R3.Pin_0
  N13: LED4.A, R4.Pin_0
  N14: S4.Pin_1, S4.Pin_2, R8.Pin_0
  N15: J1.pin2, R9.Pin_0

custom parts:
  Adafruit Feather HUZZAH ESP8266: his is the Adafruit Feather HUZZAH ESP8266 - our take on an 'all-in-one' ESP8266 WiFi development board with built in USB and battery charging. Its an ESP8266 WiFi module with all the extras you need, ready to rock! We have other boards in the Feather family, check'em out here. At the Feather HUZZAH's heart is an ESP8266 WiFi microcontroller clocked at 80 MHz and at 3.3V logic. This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
